# Fritzing sketch Lightsensor_Buttons_Wiring (saved by Fritzing 0.9.10b)
breadboards: 1

parts:
  Bauteil1 = Arduino Uno (Rev3) - ICSP
  R1 = Photocell (LDR) [package=THT]
  R2 = Resistor [tolerance=±5% power=0.25 resistance=10k package=THT]
  S1 = Momentary Switch [package=ksa_sealed_tac_switch]
  S2 = Momentary Switch [package=ksa_sealed_tac_switch]

nets:
  N1: Bauteil1.A0, R1.pin_0, R2.Pin_1
  N2: Bauteil1.D6_PWM, S2.2
  N3: Bauteil1.D7, S1.2
  N4: Bauteil1.GND, R2.Pin_0, S1.3, S2.3
  N5: Bauteil1.VIN, R1.pin_1

notes:
  https://arduinogetstarted.com/tutorials/arduino-light-sensor
  https://arduinogetstarted.com/tutorials/arduino-button
